# Fritzing sketch LYNX_CircuitBoard1 (saved by Fritzing 0.9.3b)
circuit board: 8.05058cm x 7.79105cm
breadboards: 1

parts:
  Feather_M0_WiFi = Adafruit Feather M0 WINC1500 [part_number="Adafruit #3010"]
  TC1 = Adafruit MAX31856 Thermocouple Amp [part_number="Adafruit #3263"]
  TC3 = Adafruit MAX31856 Thermocouple Amp [part_number="Adafruit #3263"]
  TC2 = Adafruit MAX31856 Thermocouple Amp [part_number="Adafruit #3263"]
  TC0 = Adafruit MAX31856 Thermocouple Amp [part_number="Adafruit #3263"]
  A0123 = Adafruit ADS1015 12Bit I2C ADC [part_number="Adafruit #1083"]
  LED1 = LED - 5mm [color="Red (633nm)" package="5 mm [THT]"]
  R1 = Resistor [tolerance=±5% resistance=220 package=THT]
  LED2 = LED - 5mm [color="Red (633nm)" package="5 mm [THT]"]
  R2 = Resistor [tolerance=±5% resistance=220 package=THT]
  LED3 = LED - 5mm [color="Red (633nm)" package="5 mm [THT]"]
  R3 = Resistor [tolerance=±5% resistance=220 package=THT]

nets:
  N1: Feather_M0_WiFi.MISO, TC1.SDI, TC3.SDI, TC2.SDI, TC0.SDI
  N2: Feather_M0_WiFi.MOSI, TC1.SDO, TC3.SDO, TC2.SDO, TC0.SDO
  N3: Feather_M0_WiFi.SCK, TC1.SCK, TC3.SCK, TC2.SCK, TC0.SCK
  GND: Feather_M0_WiFi.GND, TC1.GND, TC3.GND, TC2.GND, TC0.GND, A0123.GND, LED1.cathode, LED2.cathode, LED3.cathode
  VIN: Feather_M0_WiFi.+3V3, TC1.VIN, TC3.VIN, TC2.VIN, TC0.VIN, A0123.VDD
  N4: Feather_M0_WiFi.D13, R3.Pin_1
  N5: Feather_M0_WiFi.D12, R2.Pin_1
  N6: Feather_M0_WiFi.D11, R1.Pin_1
  N7: Feather_M0_WiFi.D10, TC2.!CS
  N8: Feather_M0_WiFi.D9, TC3.!CS
  N9: Feather_M0_WiFi.D6, TC1.!CS
  N10: Feather_M0_WiFi.D5, TC0.!CS
  N11: Feather_M0_WiFi.SCL, A0123.SCL
  N12: Feather_M0_WiFi.SDA, A0123.SDA
  N13: LED1.anode, R1.Pin_0
  N14: LED2.anode, R2.Pin_0
  N15: LED3.anode, R3.Pin_0

notes:
  LYNX
  II-VI Inc.
  CM 11/2/2017
  A3
  A2
  A0
  A1
  Mk.1.0
  Power
  WiFi
  Data

custom parts:
  Adafruit Feather M0 WINC1500: This is the Adafruit Feather M0 WiFi w/ATWINC1500 - our take on an 'all-in-one' Arduino-compatible + high speed, reliable WiFi with built in USB and battery charging. Its an Adafruit Feather M0 with a WiFi module, ready to rock! Connect your Feather to the Internet with this fine new FCC-certified WiFi module from Atmel. This 802.11bgn-capable WiFi module is the best new thing for networking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
  Adafruit MAX31856 Thermocouple Amp: Thermocouples are very sensitive, requiring a good amplifier with a cold-compensation reference, as well as calculations to handle any non-linearities. For a long time we've suggested our MAX31855K breakout, which works great but is only for K-type thermocouples. Now we're happy to offer a great new thermocouple amplifier/converter that can handle just about any type of thermocouple, and even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
  Adafruit ADS1015 12Bit I2C ADC: For microcontrollers without an analog-to-digital converter or when you want a higher-precision ADC, the ADS1015 provides 12-bit precision at 3300 samples/second over I2C. The chip can be configured as 4 single-ended input channels, or two differential channels. As a nice bonus, it even includes a programmable gain amplifier, up to x16, to help boost up smaller single/differential signals to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
